# Fritzing sketch ijn_main (saved by Fritzing 0.9.3b)
circuit board: 7.6211cm x 5.17533cm
breadboards: 1

parts:
  IchigoJam_T1 = IchigoJam T  # not connected
  TRRS1 = Audio Jack (TRRS) 3.5mm [part_number="LUMBERG JEITA RC-5325A" package="RC-5325A [SMD]"]  # not connected
  Power_plug1 = Power plug
  TRM1 = Terminal 2pin
  J1 = female pin header, 14 pins [form="♀ (female)"]
  J2 = female pin header, 14 pins [form="♀ (female)"]
  J3 = female pin header, 5 pins [form="♀ (female)"]  # not connected
  J5 = female pin header, 6 pins [form="♀ (female)"]
  A2 = AE-DRV8835-S-1  # not connected
  J4 = female pin header, 6 pins [form="♀ (female)"]
  J6 = female pin header, 1 pin [form="♀ (female)"]
  J7 = female pin header, 1 pin [form="♀ (female)"]

nets (from the pcb view):
  N1: Power_plug1.GND, J1.pin7
  N2: Power_plug1.VCC, J4.pin6
  N3: TRM1.pin_1, J4.pin5
  N4: TRM1.pin_2, J4.pin4
  N5: J1.pin8, J7.pin1
  N6: J2.pin8, J4.pin1
  N7: J2.pin10, J5.pin3
  N8: J2.pin11, J5.pin4
  N9: J5.pin1, J6.pin1

custom parts:
  IchigoJam T: IchigoJam T (IchigoJam means also strawberry jam) is a low-power, low-cost single board computer development platform. As "Kid's PC", it is developing for children's programming education. In this series, the BASIC language is activated just by turning on the power, and there is a feature that it can program immediately. Because it has I/O ports, it is easy to control electronic work, not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
  Power plug: 秋月電子通商 AE-DC-POWER-JACK-DIP(通販コードK-05148)とその互換品
  Terminal 2pin: 2-pin Terminal Block
  AE-DRV8835-S-1: DRV8835 stepping and DC motor control module.
